# Fritzing sketch MFRC522 (saved by Fritzing 0.9.3b)
breadboards: 1

parts:
  Part1 = RFID-RC522-v3
  Part2 = Arduino Nano (Rev3.0)
  Part3 = Adafruit 4-channel I2C-safe Bi-directional Logic Level Converter [part_number="Adafruit #757"]
  Part4 = Arduino Nano (Rev3.0)
  Part5 = Adafruit 4-channel I2C-safe Bi-directional Logic Level Converter [part_number="Adafruit #757"]

nets:
  N1: Part1.SDA, Part3.A4
  N2: Part1.SCK, Part3.A3
  N3: Part1.MOSI, Part3.A2
  N4: Part1.MISO, Part3.A1
  GND: Part1.GND, Part2.GND, Part3.GND
  3.3V: Part1.3.3V, Part2.3V3, Part3.LV
  N5: Part2.D10, Part3.B4
  N6: Part2.D11/MOSI, Part3.B2
  N7: Part2.D12/MISO, Part3.B1
  N8: Part2.5V, Part3.HV
  N9: Part2.D13/SCK, Part3.B3
  GND_2: Part4.GND, Part5.GND
  N10: Part4.D12/MISO, Part5.B1
  N11: Part4.5V, Part5.HV
  N12: Part4.3V3, Part5.LV

custom parts:
  RFID-RC522-v3: A simple China made RFID-RC522 Reader (6x4 cm); do check the pin labels, as this is a MFRC522 based clone.
  Adafruit 4-channel I2C-safe Bi-directional Logic Level Converter: Because the Arduino (and Basic Stamp) are 5V devices, and most modern sensors, displays, flash cards and modes are 3.3V-only, many makers find that they need to perform level shifting/conversion to protect the 3.3V device from 5V. We do have some other handy level shifters in the shop, from the DIP 74LVC245 to the fancy bi-directional TXB0108. However, neither of these are happy to work with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
